// Logisim project elevator_controller.circ as structural Verilog
module main (
);

  wire and_1_out, button_1_out, button_2_out, button_3_out, button_4_out, button_5_out, button_6_out,
       button_7_out, button_8_out, clock_1_out, n7448_1_p9, n7448_1_p10, n7448_1_p11, n7448_1_p12,
       n7448_1_p13, n7448_1_p14, n7448_1_p15, n7474_1_p5, n7474_1_p13, n7474_2_p7, n74138_1_p7, n74138_1_p10,
       n74138_1_p11, n74138_1_p12, n74138_1_p13, n74138_1_p14, n74138_1_p15, n74148_1_p5, n74148_1_p6,
       n74148_1_p15, nand_1_out, not_1_out, not_4_out, not_5_out, not_6_out, not_7_out, not_8_out, not_9_out,
       not_10_out, not_11_out, not_12_out, not_13_out, not_14_out;
  wire [2:0] n7448_1_p2, n7474_1_p6;

  Button button_1 (.out(button_1_out));
  Button button_2 (.out(button_2_out));
  Button button_3 (.out(button_3_out));
  Button button_4 (.out(button_4_out));
  Button button_5 (.out(button_5_out));
  Button button_6 (.out(button_6_out));
  Button button_7 (.out(button_7_out));
  Button button_8 (.out(button_8_out));
  not not_1 (not_1_out, button_1_out);
  not not_2 (not_1_out, button_2_out);
  not not_3 (not_1_out, button_3_out);
  not not_4 (not_4_out, button_4_out);
  not not_5 (not_5_out, button_5_out);
  not not_6 (not_6_out, button_6_out);
  not not_7 (not_7_out, button_7_out);
  // _7400_lib_74148 74148_1: pin names not known; wires that end beside it: not_4_out, not_1_out, not_1_out, not_1_out, n74148_1_p5, n74148_1_p6, 1'b0, not_1_out, not_7_out, 1'b1, not_5_out, not_6_out, not_7_out, not_7_out, n74148_1_p15
  nand nand_1 (nand_1_out, not_1_out, not_4_out, not_5_out, not_6_out, not_7_out);
  Clock clock_1 (.out(clock_1_out));
  and and_1 (and_1_out, nand_1_out, clock_1_out);
  // _7474 7474_1: pin names not known; wires that end beside it: button_8_out, n74148_1_p6, and_1_out, 1'b0, n7474_1_p5, n7474_1_p6[0], 1'b0, 1'b1, button_8_out, n74148_1_p5, and_1_out, 1'b0, n7474_1_p13, n7474_1_p6[1]
  // _7474 7474_2: pin names not known; wires that end beside it: 1'b0, 1'b1, button_8_out, n74148_1_p15, and_1_out, 1'b0, n7474_2_p7, n7474_1_p6[2]
  LED led_1 (.in(n7474_1_p13));
  LED led_2 (.in(n7474_1_p5));
  LED led_3 (.in(n7474_2_p7));
  // _7448 7448_1: pin names not known; wires that end beside it: 1'b1, n7448_1_p2[0], 1'b1, 1'b1, 1'b0, n7448_1_p2[2], 1'b0, 1'b1, n7448_1_p9, n7448_1_p10, n7448_1_p11, n7448_1_p12, n7448_1_p13, n7448_1_p14, n7448_1_p15
  // _74138 74138_1: pin names not known; wires that end beside it: n7448_1_p2[2], 1'b1, n7448_1_p2[0], 1'b0, 1'b0, 1'b1, n74138_1_p7, 1'b0, 1'b1, n74138_1_p10, n74138_1_p11, n74138_1_p12, n74138_1_p13, n74138_1_p14, n74138_1_p15
  _7_Segment_Display u_7_segment_display_1 (
    .g(n7448_1_p10), .f(n7448_1_p9), .a(n7448_1_p11), .b(n7448_1_p12), .e(n7448_1_p15), .d(n7448_1_p14),
    .c(n7448_1_p13));  // open: dp
  not not_8 (not_8_out, n74138_1_p7);
  not not_9 (not_9_out, n74138_1_p15);
  not not_10 (not_10_out, n74138_1_p14);
  not not_11 (not_11_out, n74138_1_p13);
  not not_12 (not_12_out, n74138_1_p12);
  not not_13 (not_13_out, n74138_1_p11);
  not not_14 (not_14_out, n74138_1_p10);
  LED led_4 (.in(not_8_out));
  LED led_5 (.in(not_9_out));
  LED led_6 (.in(not_10_out));
  LED led_7 (.in(not_11_out));
  LED led_8 (.in(not_12_out));
  LED led_9 (.in(not_13_out));
  LED led_10 (.in(not_14_out));
  // also tied to VCC on the sheet: not_7_out
endmodule
