// Logisim project first.circ as structural Verilog: 1 circuit, main circuit main
module main (
  input  Floor_1,
  input  Floor_2,
  input  Floor_3,
  input  Floor_4,
  input  Floor_5,
  input  Floor_6,
  input  Floor_7,
  input  Reset
);

  wire bcd_to_7_segment_decoder_1_p1, bcd_to_7_segment_decoder_1_p3, bcd_to_7_segment_decoder_1_p4,
       bcd_to_7_segment_decoder_1_p5, bcd_to_7_segment_decoder_1_p6, bcd_to_7_segment_decoder_1_p7,
       bcd_to_7_segment_decoder_1_p8, bcd_to_7_segment_decoder_1_p9, bcd_to_7_segment_decoder_1_p10,
       counter_1_p1, d_ff_1_p1, d_ff_1_p2, d_ff_2_p1, n555_timer_1_p1, n555_timer_1_p2, n555_timer_1_p3,
       n555_timer_1_p4, n555_timer_1_p5, n555_timer_1_p7, n555_timer_1_p8, n555_timer_1_p9, n555_timer_1_p13,
       n555_timer_1_p14, n555_timer_1_p15, priority_encoder_1_p1, priority_encoder_1_p2,
       priority_encoder_1_p4;

  // Priority_Encoder priority_encoder_1: pin names not known; wires that end beside it: priority_encoder_1_p1, priority_encoder_1_p2, priority_encoder_1_p1, priority_encoder_1_p4, priority_encoder_1_p2
  // D_Flip_Flop d_ff_1: pin names not known; wires that end beside it: d_ff_1_p1, d_ff_1_p2
  // D_Flip_Flop d_ff_2: pin names not known; wires that end beside it: d_ff_2_p1, d_ff_1_p1
  // D_Flip_Flop d_ff_3: pin names not known; wires that end beside it: d_ff_2_p1
  // _555_Timer 555_timer_1: pin names not known; wires that end beside it: n555_timer_1_p1, n555_timer_1_p2, n555_timer_1_p3, n555_timer_1_p4, n555_timer_1_p5, d_ff_1_p2, n555_timer_1_p7, n555_timer_1_p8, n555_timer_1_p9, n555_timer_1_p7, n555_timer_1_p8, n555_timer_1_p9, n555_timer_1_p13, n555_timer_1_p14, n555_timer_1_p15
  Comparator comparator_1 (.eq(n555_timer_1_p13));  // open: a, b, gt, lt
  // AND_Gate and_1: pin names not known; wires that end beside it: n555_timer_1_p14
  // AND_Gate and_2: pin names not known; wires that end beside it: n555_timer_1_p15
  // Counter counter_1: pin names not known; wires that end beside it: counter_1_p1, counter_1_p1
  // BCD_to_7_Segment_Decoder bcd_to_7_segment_decoder_1: pin names not known; wires that end beside it: bcd_to_7_segment_decoder_1_p1, bcd_to_7_segment_decoder_1_p1, bcd_to_7_segment_decoder_1_p3, bcd_to_7_segment_decoder_1_p4, bcd_to_7_segment_decoder_1_p5, bcd_to_7_segment_decoder_1_p6, bcd_to_7_segment_decoder_1_p7, bcd_to_7_segment_decoder_1_p8, bcd_to_7_segment_decoder_1_p9, bcd_to_7_segment_decoder_1_p10
  // _7_Segment_Display 7_segment_display_1: pin names not known; wires that end beside it: bcd_to_7_segment_decoder_1_p10
  LED led_1 (.in(bcd_to_7_segment_decoder_1_p3));
  LED led_2 (.in(bcd_to_7_segment_decoder_1_p4));
  LED led_3 (.in(bcd_to_7_segment_decoder_1_p5));
  LED led_4 (.in(bcd_to_7_segment_decoder_1_p9));
  LED led_5 (.in(bcd_to_7_segment_decoder_1_p6));
  LED led_6 (.in(bcd_to_7_segment_decoder_1_p7));
  LED led_7 (.in(bcd_to_7_segment_decoder_1_p8));
endmodule
